# Fritzing sketch Fritzing Sketch Source File (saved by Fritzing 0.9.3b)

parts:
  Part2 = Arduino Uno (Rev3)
  U2 = LCD-16X2 [package=lcd-16x2]
  LCM1602_IIC2 = LCM1602 IIC [part_number="LCM1602 IIC" chip_label="LCM1602 IIC" package="DIP (Dual Inline) [THT]"]
  J1 = Piezo Speaker
  e-radionica_com1 = LM393 vibration sensor breakout [part_number=100031]

nets:
  N1: Part2.A0, e-radionica_com1.AO
  N2: Part2.A4/SDA, LCM1602_IIC2.SDA
  N3: Part2.A5/SCL, LCM1602_IIC2.SCL
  GND: Part2.GND, LCM1602_IIC2.GND, J1.pin1, e-radionica_com1.GND
  N4: Part2.D7, J1.pin2
  VCC: Part2.5V, LCM1602_IIC2.VCC, e-radionica_com1.VCC
  N5: U2.VSS, LCM1602_IIC2.K
  N6: U2.VDD, LCM1602_IIC2.A
  N7: U2.VO, LCM1602_IIC2.D7
  N8: U2.RS, LCM1602_IIC2.D6
  N9: U2.R_W, LCM1602_IIC2.D5
  N10: U2.E, LCM1602_IIC2.D4
  N11: U2.DB0, LCM1602_IIC2.D3
  N12: U2.DB1, LCM1602_IIC2.D2
  N13: U2.DB2, LCM1602_IIC2.D1
  N14: U2.DB3, LCM1602_IIC2.D0
  N15: U2.DB4, LCM1602_IIC2.E
  N16: U2.DB5, LCM1602_IIC2.RW
  N17: U2.DB6, LCM1602_IIC2.RS
  N18: U2.DB7, LCM1602_IIC2.V0
  N19: U2.A, LCM1602_IIC2.VDD
  N20: U2.K, LCM1602_IIC2.VSS

notes:
  GND - Green
  5VC - Red
  GPIO - Blue
  Developed By Web Dev Fusion
  www.webdevfusion.com

custom parts:
  LCM1602 IIC: I2C-Module to use a 1602 or 2004 LCD on with the wire.h libory Serial LCD Modul
